// Logisim project CPUfromScratch.circ as structural Verilog: 9 circuits, main circuit main
module main (
  input  in_1,
  input  [1:0] in_2,
  output out_3,
  output out_4,
  output out_5,
  output out_6
);

  Decoder #(.select(2)) decoder_1 (.out0(out_3), .out1(out_4), .out2(out_5), .out3(out_6), .sel(in_2), .en(in_1));
endmodule

module OneBitMemory (
  input  i,
  input  s,
  output o
);

  wire a_out, b_out, c_out, d_out;

  nand a (a_out, i, s);
  nand b (b_out, a_out, s);
  nand d (d_out, c_out, b_out);
  nand c (c_out, a_out, d_out);
endmodule

module EightBitMemory (
  input  in_1,
  input  [7:0] in_2,
  output [7:0] out_3
);

  wire [7:0] onebitmemory_1_o;

  OneBitMemory onebitmemory_1 (.i(in_2[0]), .s(in_1), .o(onebitmemory_1_o[0]));
  OneBitMemory onebitmemory_2 (.i(in_2[1]), .s(in_1), .o(onebitmemory_1_o[1]));
  OneBitMemory onebitmemory_3 (.i(in_2[2]), .s(in_1), .o(onebitmemory_1_o[2]));
  OneBitMemory onebitmemory_4 (.i(in_2[3]), .s(in_1), .o(onebitmemory_1_o[3]));
  OneBitMemory onebitmemory_5 (.i(in_2[4]), .s(in_1), .o(onebitmemory_1_o[4]));
  OneBitMemory onebitmemory_6 (.i(in_2[5]), .s(in_1), .o(onebitmemory_1_o[5]));
  OneBitMemory onebitmemory_7 (.i(in_2[6]), .s(in_1), .o(onebitmemory_1_o[6]));
  OneBitMemory onebitmemory_8 (.i(in_2[7]), .s(in_1), .o(onebitmemory_1_o[7]));
endmodule

module Register8 (
  input  in_1,
  input  [7:0] in_2,
  input  in_3,
  output [7:0] out_4
);

  wire undriven;
  wire [7:0] controlled_buffer_1_out, controlled_buffer_2_out, eightbitmemory_1_out_3, enablerand_1_out_3;

  assign controlled_buffer_1_out = in_1 ? in_2 : 8'bz;  // Controlled_Buffer controlled_buffer_1
  EightBitMemory eightbitmemory_1 (.in_1(in_1), .in_2(controlled_buffer_1_out), .out_3(eightbitmemory_1_out_3));
  EnablerAnd enablerand_1 (.in_1(eightbitmemory_1_out_3), .in_2(undriven), .out_3(enablerand_1_out_3));
  assign controlled_buffer_2_out = undriven ? enablerand_1_out_3 : 8'bz;  // Controlled_Buffer controlled_buffer_2
endmodule

module EnablerAnd (
  input  [7:0] in_1,
  input  in_2,
  output [7:0] out_3
);

  and and_1 (out_3[0], in_2, in_1[0]);
  and and_2 (out_3[1], in_2, in_1[1]);
  and and_3 (out_3[2], in_2, in_1[2]);
  and and_4 (out_3[3], in_2, in_1[3]);
  and and_5 (out_3[4], in_2, in_1[4]);
  and and_6 (out_3[5], in_2, in_1[5]);
  and and_7 (out_3[6], in_2, in_1[6]);
  and and_8 (out_3[7], in_2, in_1[7]);

  // Notes on the sheet:
  //   If set is 0, all output is 0; control to send output to bus or not 
endmodule

module bus_ex (
  input  in_1,
  input  in_2,
  input  in_3,
  input  in_4,
  input  [7:0] in_5,
  output [7:0] out_6,
  output [7:0] out_7,
  output [7:0] out_8
);

  wire and_1_out, not_1_out, not_2_out;

  not not_1 (not_1_out, in_4);
  not not_2 (not_2_out, in_3);
  and and_1 (and_1_out, not_1_out, not_2_out);
  assign out_8 = and_1_out ? in_5 : 8'bz;  // Controlled_Buffer inBuffer
  Register8 RegisterA (.in_1(in_1), .in_2(out_8), .in_3(in_3), .out_4(out_7));
  assign out_8 = in_3 ? out_7 : 8'bz;  // Controlled_Buffer outBufferA
  Register8 RegisterB (.in_1(in_2), .in_2(out_8), .in_3(in_4), .out_4(out_6));
  assign out_8 = in_4 ? out_6 : 8'bz;  // Controlled_Buffer outBufferB

  // Notes on the sheet:
  //   Use Controll buffer to avoid collision. Copy data in Register A to B: Set 1 in Register A to put the data in register A > Set 0 > Enabler 1 > whlle Enabler 1, then bus fills with data, set 1 in register B and Set 0 in register B and Enabler 0 for Register A, Enabler 1 for Register B 
endmodule

module Decoder3x8 (
  input  in_1,
  input  in_2,
  input  in_3,
  output out_4,
  output out_5,
  output out_6,
  output out_7,
  output out_8,
  output out_9,
  output out_10,
  output out_11
);

  wire not_1_out, not_2_out, not_3_out;

  not not_1 (not_1_out, in_1);
  not not_2 (not_2_out, in_2);
  not not_3 (not_3_out, in_3);
  and and_1 (out_4, not_1_out, not_2_out, not_3_out);
  and and_2 (out_5, not_1_out, not_2_out, in_3);
  and and_3 (out_6, not_1_out, in_2, not_3_out);
  and and_4 (out_7, not_1_out, in_2, in_3);
  and and_5 (out_8, in_1, not_2_out, not_3_out);
  and and_6 (out_9, in_1, not_2_out, in_3);
  and and_7 (out_10, in_1, in_2, not_3_out);
  and and_8 (out_11, in_1, in_2, in_3);
endmodule

module RAM1 (
  input  Y,
  input  X,
  input  bus_set,
  input  bus_enable,
  input  [7:0] bus_in,
  output [7:0] bus_out
);

  wire and_add_out, and_enbl_out, and_set_out;
  wire [7:0] controlled_buffer_1_out, register8_1_out_4;

  and and_add (and_add_out, Y, X);
  assign controlled_buffer_1_out = and_add_out ? bus_in : 8'bz;  // Controlled_Buffer controlled_buffer_1
  assign bus_out = and_add_out ? register8_1_out_4 : 8'bz;  // Controlled_Buffer controlled_buffer_2
  and and_set (and_set_out, and_add_out, bus_set);
  and and_enbl (and_enbl_out, and_add_out, bus_enable);
  Register8 register8_1 (
    .in_1(and_set_out), .in_2(controlled_buffer_1_out), .in_3(and_enbl_out), .out_4(register8_1_out_4));
endmodule

module EnablerInv (
  input  [7:0] in_1,
  input  in_2,
  output [7:0] out_3
);

  assign out_3 = in_2 ? in_1 : 8'bz;  // Controlled_Buffer controlled_buffer_1
endmodule
